# Fritzing sketch Solar_tracker (saved by Fritzing 0.9.3b)
breadboards: 1

parts:
  Arduino = Arduino Uno (Rev3)
  R1 = Resistor [tolerance=±5% resistance=10k package=THT]
  R2 = Resistor [tolerance=±5% resistance=4.7k package=THT]
  R3 = Resistor [tolerance=±5% resistance=10k package=THT]
  R4 = Resistor [tolerance=±5% resistance=4.7k package=THT]
  Lead_Acid_Battery = DC Power [voltage=12V]
  Plug_from_Panel = Power plug
  Buck/Boost_Converter = IC, DIP package, 4 pins [chip_label=IC]
  R5 = Photocell (LDR) [package=THT]
  R6 = Photocell (LDR) [package=THT]
  R7 = Resistor [tolerance=±5% resistance=10k package=THT]
  R8 = Resistor [tolerance=±5% resistance=10k package=THT]

nets:
  N1: Arduino.A0, R5.pin_0, R7.Pin_1
  N2: Arduino.A1, R6.pin_0, R8.Pin_1
  PanelV: Arduino.A2, R1.Pin_1, R2.Pin_0
  Battery: Arduino.A3, R3.Pin_1, R4.Pin_0
  N3: Arduino.5V, R7.Pin_0, R8.Pin_0
  GND: Arduino.GND, R2.Pin_1, R4.Pin_1, Lead_Acid_Battery.V-, Plug_from_Panel.GND, Buck/Boost_Converter.pin2, Buck/Boost_Converter.pin3, R5.pin_1, R6.pin_1
  N4: Arduino.VIN, R3.Pin_0, Lead_Acid_Battery.V+, Buck/Boost_Converter.pin4
  N5: R1.Pin_0, Plug_from_Panel.VCC, Buck/Boost_Converter.pin1
